// Logisim project BraiNIAC.circ as structural Verilog
module main (
);

  wire counter_controller_1_count, counter_controller_1_load;
  wire [3:0] multiplexer_1_out, register_1_q;
  wire [7:0] rom_1_data;
  wire [15:0] counter_1_q, counter_controller_1_data_2;

  Counter_Controller counter_controller_1 (
    .LOAD(counter_controller_1_load), .Data_2(counter_controller_1_data_2), .COUNT(counter_controller_1_count));  // open: UP, Data, DOWN
  Counter #(.width(16), .max('hffff)) counter_1 (
    .load(counter_controller_1_load), .D(counter_controller_1_data_2), .count(counter_controller_1_count),
    .Q(counter_1_q));  // open: carry, clk, clr
  ROM #(.addrWidth(15)) rom_1 (.addr(counter_1_q[14:0]), .data(rom_1_data));  // open: sel
  Multiplexer #(.width(4)) multiplexer_1 (
    .in0(rom_1_data[3:0]), .in1(rom_1_data[7:4]), .out(multiplexer_1_out), .sel(counter_1_q[15]));  // open: en
  Register #(.width(4), .trigger("high")) register_1 (.D(multiplexer_1_out), .Q(register_1_q));  // open: en, clk, clr
  Decoder #(.select(3)) decoder_1 (.sel(register_1_q[2:0]));  // open: out0, out1, out2, out3, out4, out5, out6, out7, en

  // Notes on the sheet:
  //   Program Counter
  //   Program Memory
  //   Instruction Register
  //   Instruction Decoder
endmodule

module Counter_Controller (
  input  UP,
  input  [15:0] Data,
  input  DOWN,
  output LOAD,
  output [15:0] Data_2,
  output COUNT
);

  wire and_2_out, and_3_out, not_1_out, not_2_out, not_3_out;

  not not_1 (not_1_out, UP);
  not not_2 (not_2_out, UP);
  not not_3 (not_3_out, DOWN);
  and and_1 (LOAD, not_1_out, DOWN);
  and and_2 (and_2_out, not_2_out, DOWN);
  and and_3 (and_3_out, UP, not_3_out);
  or or_1 (COUNT, and_2_out, and_3_out);

  assign Data_2 = Data;
endmodule
